# Fritzing sketch barca (saved by Fritzing 0.9.3b)

parts:
  Part1 = Arduino Nano (Rev3.0)
  Part2 = Thumb Joystick
  Part3 = NRF24L01+ Breakout Board
  Power_plug1 = Power plug

nets:
  GND: Part1.GND, Part2.GND, Part3.GND, Power_plug1.GND
  N1: Part1.D9, Part3.CS
  N2: Part1.D10, Part3.CE
  N3: Part1.D11/MOSI, Part3.MOSI
  N4: Part1.D12/MISO, Part3.MISO
  VCC: Part1.5V, Part2.VCC, Power_plug1.VCC
  N5: Part1.A1, Part2.VERT
  N6: Part1.A0, Part2.HORZ
  3V3: Part1.3V3, Part3.VCC
  N7: Part1.D13/SCK, Part3.SCK
